// Logisim project prob1_1a.circ as structural Verilog: 1 circuit, main circuit main
module main (
  input  a,
  input  a2,
  input  b,
  input  b2,
  input  c,
  input  c2,
  output out2,
  output res
);

  wire and_1_out, and_2_out, and_3_out, and_4_out, and_5_out, n7408_1_pin3, n7408_1_pin6, n7408_1_pin8,
       n7411_1_pin12, n7432_1_pin3, n7432_1_pin5, or_1_out, or_2_out;

  Clock clk ();  // open: out
  and and_1 (and_1_out, b, a);
  and and_2 (and_2_out, a, b);
  and and_3 (and_3_out, b, c);
  and and_4 (and_4_out, a, c);
  and and_5 (and_5_out, and_1_out, c);
  or or_1 (or_1_out, and_5_out, and_2_out);
  or or_2 (or_2_out, and_3_out, and_4_out);
  or or_3 (res, or_1_out, or_2_out);
  _7411 u_7411_1 (
    .pin1(b2), .pin2(c2), .pin13(a2), .pin12(n7411_1_pin12));  // open: pin3, pin4, pin5, pin6, pin11, pin10, pin9, pin8
  _7408 u_7408_1 (
    .pin1(a2), .pin2(b2), .pin3(n7408_1_pin3), .pin4(a2), .pin5(c2), .pin6(n7408_1_pin6), .pin10(b2),
    .pin9(c2), .pin8(n7408_1_pin8));  // open: pin13, pin12, pin11
  _7432 u_7432_1 (
    .pin1(n7408_1_pin6), .pin2(n7408_1_pin3), .pin3(n7432_1_pin3), .pin4(n7432_1_pin3), .pin5(n7432_1_pin5),
    .pin6(out2), .pin10(n7408_1_pin8), .pin9(n7411_1_pin12), .pin8(n7432_1_pin5));  // open: pin13, pin12, pin11
endmodule
