// Logisim project prob1_1b.circ as structural Verilog: 1 circuit, main circuit main
module main (
  input  a1,
  input  a2,
  input  b1,
  input  b2,
  input  c1,
  input  c2,
  output out1,
  output out2
);

  wire and_1_out, and_2_out, and_3_out, and_4_out, and_5_out, n7404_1_pin2, n7404_1_pin10, n7404_1_pin12,
       n7408_1_pin11, n7411_1_pin6, n7411_1_pin12, n7432_1_pin3, not_1_out, not_2_out, not_3_out, or_1_out;

  Clock clock_1 ();  // open: out
  not not_1 (not_1_out, a1);
  not not_2 (not_2_out, b1);
  and and_1 (and_1_out, not_1_out, b1);
  not not_3 (not_3_out, c1);
  and and_2 (and_2_out, a1, not_2_out);
  and and_3 (and_3_out, not_1_out, not_2_out);
  and and_4 (and_4_out, and_1_out, not_3_out);
  and and_5 (and_5_out, and_2_out, not_3_out);
  or or_1 (or_1_out, and_3_out, and_4_out);
  or or_2 (out1, or_1_out, and_5_out);
  _7404 u_7404_1 (
    .pin1(c2), .pin2(n7404_1_pin2), .pin13(b2), .pin12(n7404_1_pin12), .pin11(a2), .pin10(n7404_1_pin10));  // open: pin3, pin4, pin5, pin6, pin9, pin8
  _7408 u_7408_1 (
    .pin13(n7404_1_pin10), .pin12(n7404_1_pin12), .pin11(n7408_1_pin11));  // open: pin1, pin2, pin3, pin4, pin5, pin6, pin10, pin9, pin8
  _7411 u_7411_1 (
    .pin1(n7404_1_pin10), .pin2(n7404_1_pin2), .pin3(n7404_1_pin2), .pin4(n7404_1_pin12), .pin5(a2),
    .pin6(n7411_1_pin6), .pin13(b2), .pin12(n7411_1_pin12));  // open: pin11, pin10, pin9, pin8
  _7432 u_7432_1 (
    .pin1(n7411_1_pin12), .pin2(n7411_1_pin6), .pin3(n7432_1_pin3), .pin13(n7408_1_pin11),
    .pin12(n7432_1_pin3), .pin11(out2));  // open: pin4, pin5, pin6, pin10, pin9, pin8
endmodule
