// Logisim project prob2_decoder.circ as structural Verilog: 1 circuit, main circuit main
module main (
  input  in0,
  input  in1,
  input  in2,
  output segment_a,
  output segment_b,
  output segment_c,
  output segment_d,
  output segment_e,
  output segment_f,
  output segment_g
);

  wire and_1_out, and_2_out, and_3_out, and_4_out, and_5_out, and_6_out, and_7_out, car0_out, car1_out,
       car2_out, car3_out, car4_out, car5_out, car6_out, not_1_out, not_2_out, not_3_out, or_1_out, or_2_out,
       or_3_out, or_4_out, or_5_out, or_6_out, or_7_out, or_8_out, or_9_out, or_10_out, or_11_out, or_12_out,
       or_13_out, or_14_out, or_15_out, or_16_out, or_17_out, or_18_out, or_19_out, or_20_out, or_21_out,
       or_22_out, or_23_out, or_24_out, or_25_out, or_26_out, or_27_out, or_28_out;

  not not_1 (not_1_out, in0);
  not not_2 (not_2_out, in1);
  not not_3 (not_3_out, in2);
  and and_1 (and_1_out, in0, not_2_out);
  and and_2 (and_2_out, not_1_out, in1);
  and and_3 (and_3_out, in0, in1);
  and and_4 (and_4_out, not_2_out, in2);
  and and_5 (and_5_out, not_2_out, in2);
  and and_6 (and_6_out, in1, in2);
  and and_7 (and_7_out, in1, in2);
  and car0 (car0_out, and_1_out, not_3_out);
  and car1 (car1_out, and_2_out, not_3_out);
  and car2 (car2_out, and_3_out, not_3_out);
  and car3 (car3_out, and_4_out, not_1_out);
  and car4 (car4_out, and_5_out, in0);
  and car5 (car5_out, and_6_out, not_1_out);
  and car6 (car6_out, and_7_out, in0);
  or or_1 (or_1_out, car0_out, car2_out);
  or or_2 (or_2_out, car3_out, car5_out);
  buf or_3 (or_3_out, car6_out);  // OR_Gate
  or or_4 (or_4_out, car0_out, car1_out);
  or or_5 (or_5_out, car2_out, car3_out);
  buf or_6 (or_6_out, car4_out);  // OR_Gate
  or or_7 (or_7_out, car0_out, car1_out);
  or or_8 (or_8_out, car3_out, car4_out);
  or or_9 (or_9_out, car5_out, car6_out);
  or or_10 (or_10_out, car0_out, car2_out);
  or or_11 (or_11_out, car3_out, car5_out);
  buf or_12 (or_12_out, car6_out);  // OR_Gate
  buf or_13 (or_13_out, car0_out);  // OR_Gate
  buf or_14 (or_14_out, car2_out);  // OR_Gate
  buf or_15 (or_15_out, car6_out);  // OR_Gate
  or or_16 (or_16_out, car0_out, car4_out);
  buf or_17 (or_17_out, car5_out);  // OR_Gate
  buf or_18 (or_18_out, car6_out);  // OR_Gate
  or or_19 (or_19_out, car2_out, car3_out);
  or or_20 (or_20_out, car4_out, car5_out);
  buf or_21 (or_21_out, car6_out);  // OR_Gate
  or or_22 (or_22_out, or_1_out, or_2_out);
  or or_23 (or_23_out, or_4_out, or_5_out);
  or or_24 (or_24_out, or_7_out, or_8_out);
  or or_25 (or_25_out, or_10_out, or_11_out);
  or or_26 (or_26_out, or_13_out, or_14_out);
  or or_27 (or_27_out, or_16_out, or_17_out);
  or or_28 (or_28_out, or_19_out, or_20_out);
  or or_29 (segment_a, or_22_out, or_3_out);
  or or_30 (segment_b, or_23_out, or_6_out);
  or or_31 (segment_c, or_24_out, or_9_out);
  or or_32 (segment_d, or_25_out, or_12_out);
  or or_33 (segment_e, or_26_out, or_15_out);
  or or_34 (segment_f, or_27_out, or_18_out);
  or or_35 (segment_g, or_28_out, or_21_out);
endmodule
