// Logisim project prob2_encoder.circ as structural Verilog: 1 circuit, main circuit main
module main (
  input  car0,
  input  car1,
  input  car2,
  input  car3,
  input  car4,
  input  car5,
  input  car6,
  output bit0,
  output bit1,
  output bit2
);

  wire or_1_out, or_2_out, or_3_out, or_4_out, or_5_out, or_6_out;

  or or_1 (or_1_out, car0, car2);
  or or_2 (or_2_out, car4, car6);
  or or_3 (or_3_out, car1, car2);
  or or_4 (or_4_out, car5, car6);
  or or_5 (or_5_out, car5, car3);
  or or_6 (or_6_out, car4, car6);
  or or_7 (bit0, or_1_out, or_2_out);
  or or_8 (bit1, or_3_out, or_4_out);
  or or_9 (bit2, or_5_out, or_6_out);
endmodule
