// Logisim project prob2_system.circ as structural Verilog: 1 circuit, main circuit main
module main (
  input  in0,
  input  in1,
  input  in2,
  input  car0,
  input  car1,
  input  car2,
  input  car3,
  input  car4,
  input  car5,
  input  car6,
  output bit0,
  output segment_a,
  output bit1,
  output segment_b,
  output bit2,
  output segment_c,
  output segment_d,
  output segment_e,
  output segment_f,
  output segment_g
);

  wire and_1_out, and_2_out, and_3_out, and_4_out, and_5_out, and_6_out, and_7_out, and_8_out, and_9_out,
       and_10_out, and_11_out, and_12_out, and_13_out, and_14_out, not_1_out, not_2_out, not_3_out, or_1_out,
       or_2_out, or_3_out, or_4_out, or_5_out, or_6_out, or_10_out, or_11_out, or_12_out, or_13_out,
       or_14_out, or_15_out, or_16_out, or_17_out, or_18_out, or_19_out, or_20_out, or_21_out, or_22_out,
       or_23_out, or_24_out, or_25_out, or_26_out, or_27_out, or_28_out, or_29_out, or_30_out, or_31_out,
       or_32_out, or_33_out, or_34_out, or_35_out, or_36_out, or_37_out;

  or or_1 (or_1_out, car0, car2);
  or or_2 (or_2_out, car4, car6);
  or or_3 (or_3_out, car1, car2);
  or or_4 (or_4_out, car5, car6);
  or or_5 (or_5_out, car5, car3);
  or or_6 (or_6_out, car4, car6);
  or or_7 (bit0, or_1_out, or_2_out);
  or or_8 (bit1, or_3_out, or_4_out);
  or or_9 (bit2, or_5_out, or_6_out);
  not not_1 (not_1_out, bit0);
  not not_2 (not_2_out, bit1);
  not not_3 (not_3_out, bit2);
  and and_1 (and_1_out, bit0, not_2_out);
  and and_2 (and_2_out, and_1_out, not_3_out);
  and and_3 (and_3_out, not_1_out, bit1);
  and and_4 (and_4_out, and_3_out, not_3_out);
  and and_5 (and_5_out, bit0, bit1);
  and and_6 (and_6_out, and_5_out, not_3_out);
  and and_7 (and_7_out, not_2_out, bit2);
  and and_8 (and_8_out, and_7_out, not_1_out);
  and and_9 (and_9_out, not_2_out, bit2);
  and and_10 (and_10_out, and_9_out, bit0);
  and and_11 (and_11_out, bit1, bit2);
  and and_12 (and_12_out, and_11_out, not_1_out);
  and and_13 (and_13_out, bit1, bit2);
  and and_14 (and_14_out, and_13_out, bit0);
  or or_10 (or_10_out, and_2_out, and_6_out);
  or or_11 (or_11_out, and_8_out, and_12_out);
  buf or_12 (or_12_out, and_14_out);  // OR_Gate
  or or_13 (or_13_out, and_2_out, and_4_out);
  or or_14 (or_14_out, and_6_out, and_8_out);
  buf or_15 (or_15_out, and_10_out);  // OR_Gate
  or or_16 (or_16_out, and_2_out, and_4_out);
  or or_17 (or_17_out, and_8_out, and_10_out);
  or or_18 (or_18_out, and_12_out, and_14_out);
  or or_19 (or_19_out, and_2_out, and_6_out);
  or or_20 (or_20_out, and_8_out, and_12_out);
  buf or_21 (or_21_out, and_14_out);  // OR_Gate
  buf or_22 (or_22_out, and_2_out);  // OR_Gate
  buf or_23 (or_23_out, and_6_out);  // OR_Gate
  buf or_24 (or_24_out, and_14_out);  // OR_Gate
  or or_25 (or_25_out, and_2_out, and_10_out);
  buf or_26 (or_26_out, and_12_out);  // OR_Gate
  buf or_27 (or_27_out, and_14_out);  // OR_Gate
  or or_28 (or_28_out, and_6_out, and_8_out);
  or or_29 (or_29_out, and_10_out, and_12_out);
  buf or_30 (or_30_out, and_14_out);  // OR_Gate
  or or_31 (or_31_out, or_10_out, or_11_out);
  or or_32 (or_32_out, or_13_out, or_14_out);
  or or_33 (or_33_out, or_16_out, or_17_out);
  or or_34 (or_34_out, or_19_out, or_20_out);
  or or_35 (or_35_out, or_22_out, or_23_out);
  or or_36 (or_36_out, or_25_out, or_26_out);
  or or_37 (or_37_out, or_28_out, or_29_out);
  or or_38 (segment_a, or_31_out, or_12_out);
  or or_39 (segment_b, or_32_out, or_15_out);
  or or_40 (segment_c, or_33_out, or_18_out);
  or or_41 (segment_d, or_34_out, or_21_out);
  or or_42 (segment_e, or_35_out, or_24_out);
  or or_43 (segment_f, or_36_out, or_27_out);
  or or_44 (segment_g, or_37_out, or_30_out);
  _7_Segment_Display u_7_segment_display_1 (
    .g(segment_g), .f(segment_f), .a(segment_a), .b(segment_b), .e(segment_e), .d(segment_d), .c(segment_c));  // open: dp

  // Notes on the sheet:
  //   encoder
  //   decoder
endmodule
