// Logisim project prob2.circ as structural Verilog: 1 circuit, main circuit main
module main (
  input  in_1,
  output out_2,
  output out_3
);

  wire and_1_out, and_2_out, and_3_out, and_4_out, button_1_out, button_2_out, clk_out, clock_1_out,
       clock_2_out, d_ff_1_q, nand_1_out, nand_2_out, nand_3_out, nand_4_out, nand_5_out, nand_6_out,
       nand_8_out, nor_1_out, nor_2_out, nor_4_out, not_1_out, not_2_out, not_3_out, not_4_out, undriven,
       xor_2_out, xor_3_out;

  Button button_1 (.out(button_1_out));
  // XOR_Gate xor_1 has open pins: in0=out_2, in1=in_1, out=open
  Clock clock_1 (.out(clock_1_out));
  Clock clock_2 (.out(clock_2_out));
  not not_1 (not_1_out, undriven);
  D_Flip_Flop d_ff_1 (.D(xor_2_out), .clk(clock_2_out), .Q(d_ff_1_q));  // open: Qn, preset, reset
  xor xor_2 (xor_2_out, d_ff_1_q, button_1_out);
  and and_1 (and_1_out, undriven, clock_1_out);
  and and_2 (and_2_out, clock_1_out, not_1_out);
  nor nor_1 (nor_1_out, and_1_out, nor_2_out);
  nor nor_2 (nor_2_out, nor_1_out, and_2_out);
  not not_2 (not_2_out, nor_2_out);
  Button button_2 (.out(button_2_out));
  xor xor_3 (xor_3_out, out_3, button_2_out);
  Clock clk (.out(clk_out));
  and and_3 (and_3_out, nor_2_out, clock_1_out);
  and and_4 (and_4_out, clock_1_out, not_2_out);
  not not_3 (not_3_out, xor_3_out);
  nor nor_3 (out_2, and_3_out, nor_4_out);
  nor nor_4 (nor_4_out, out_2, and_4_out);
  nand nand_1 (nand_1_out, xor_3_out, clk_out);
  nand nand_2 (nand_2_out, not_3_out, clk_out);
  nand nand_3 (nand_3_out, nand_1_out, nand_4_out);
  nand nand_4 (nand_4_out, nand_3_out, nand_2_out);
  not not_4 (not_4_out, clk_out);
  nand nand_5 (nand_5_out, nand_3_out, not_4_out);
  nand nand_6 (nand_6_out, not_4_out, nand_4_out);
  nand nand_7 (out_3, nand_5_out, nand_8_out);
  nand nand_8 (nand_8_out, out_3, nand_6_out);

  // Notes on the sheet:
  //   replace w/ 7486: quad 2-input XOR gate
  //   replace 2 inverters with 7414: Hex Inverter
  //   replace the 8 NAND gates w 2copies of 7424: quad 2-input NAND gate
endmodule
