// Logisim project prob3.circ as structural Verilog: 1 circuit, main circuit main
// clk
module main (
  input  io,
  input  a3,
  input  a2,
  input  a1,
  input  a0,
  output out_6,
  output out_7,
  output out_8,
  output out_9,
  output out_10,
  output out_11,
  output out_12,
  output AC,
  output D0,
  output D1,
  output D2,
  output D3,
  output Engine,
  output Wipers
);

  wire and_1_out, and_2_out, and_3_out, and_4_out, and_5_out, and_6_out, and_7_out, and_8_out, and_9_out,
       and_10_out, and_11_out, and_12_out, and_13_out, and_14_out, and_15_out, and_16_out, and_17_out,
       and_18_out, and_19_out, and_20_out, and_21_out, and_22_out, and_23_out, and_24_out, and_25_out,
       and_26_out, and_27_out, and_28_out, and_29_out, clock_1_out, multiplexer_1_out, multiplexer_2_out,
       multiplexer_3_out, multiplexer_4_out, multiplexer_5_out, multiplexer_6_out, multiplexer_7_out,
       nand_1_out, nand_2_out, nand_3_out, nand_4_out, nand_5_out, nand_6_out, nand_7_out, nand_8_out,
       nand_9_out, nand_10_out, nand_11_out, nand_12_out, nand_13_out, nand_14_out, nand_15_out, nand_16_out,
       nand_17_out, nand_18_out, nand_19_out, nand_20_out, nand_21_out, nand_22_out, nand_23_out,
       nand_24_out, nand_25_out, nand_26_out, nand_27_out, nand_28_out, nand_29_out, nand_30_out,
       nand_31_out, nand_32_out, nand_33_out, nand_34_out, nand_35_out, nand_36_out, nand_37_out,
       nand_38_out, nand_39_out, nand_40_out, nand_41_out, nand_42_out, nand_44_out, nand_46_out,
       nand_48_out, nand_50_out, nand_52_out, nand_54_out, nand_56_out, not_1_out, not_2_out, not_3_out,
       not_4_out, not_5_out, not_6_out, not_7_out, not_8_out, not_9_out, not_10_out, not_11_out, not_12_out,
       not_13_out, not_14_out, not_15_out, not_16_out, not_17_out, not_18_out, not_19_out, not_20_out,
       not_21_out, not_22_out, not_23_out, not_24_out, not_25_out, not_26_out, not_27_out, not_28_out,
       not_29_out, not_30_out, not_31_out, not_32_out, not_33_out, not_34_out, not_35_out, not_36_out,
       not_37_out, not_38_out, not_39_out, or_1_out, undriven, undriven_2, undriven_3, undriven_4,
       undriven_5, undriven_6;

  Clock clock_1 (.out(clock_1_out));
  not not_1 (not_1_out, undriven_4);
  not not_2 (not_2_out, undriven);
  not not_3 (not_3_out, undriven_3);
  not not_4 (not_4_out, undriven_4);
  not not_5 (not_5_out, undriven);
  not not_6 (not_6_out, undriven_4);
  not not_7 (not_7_out, undriven_3);
  not not_8 (not_8_out, undriven_4);
  not not_9 (not_9_out, undriven);
  not not_10 (not_10_out, undriven_3);
  not not_11 (not_11_out, undriven);
  not not_12 (not_12_out, a2);
  not not_13 (not_13_out, a1);
  not not_14 (not_14_out, a0);
  not not_15 (not_15_out, a2);
  not not_16 (not_16_out, a1);
  not not_17 (not_17_out, a2);
  not not_18 (not_18_out, a0);
  not not_19 (not_19_out, a2);
  not not_20 (not_20_out, a1);
  not not_21 (not_21_out, a0);
  not not_22 (not_22_out, a1);
  not not_23 (not_23_out, a0);
  and and_1 (and_1_out, not_1_out, not_2_out, not_3_out);
  and and_2 (and_2_out, not_4_out, not_5_out, undriven_3);
  and and_3 (and_3_out, not_6_out, undriven, not_7_out);
  and and_4 (and_4_out, not_8_out, undriven, undriven_3);
  and and_5 (and_5_out, undriven_4, not_9_out, not_10_out);
  and and_6 (and_6_out, undriven_4, not_11_out, undriven_3);
  and and_7 (and_7_out, undriven_4, undriven, undriven_5);
  and and_8 (and_8_out, not_12_out, not_13_out, io, not_14_out);
  and and_9 (and_9_out, not_15_out, not_16_out, io, a0);
  and and_10 (and_10_out, not_17_out, a1, io, not_18_out);
  and and_11 (and_11_out, not_19_out, a1, io, a0);
  and and_12 (and_12_out, a2, not_20_out, io, not_21_out);
  and and_13 (and_13_out, a2, not_22_out, io, a0);
  and and_14 (and_14_out, a2, a1, io, not_23_out);
  and and_15 (and_15_out, and_1_out, undriven_6);
  and and_16 (and_16_out, and_2_out, undriven_6);
  and and_17 (and_17_out, and_3_out, undriven_6);
  and and_18 (and_18_out, and_4_out, undriven_6);
  and and_19 (and_19_out, and_5_out, undriven_6);
  and and_20 (and_20_out, and_6_out, undriven_6);
  and and_21 (and_21_out, and_7_out, undriven_6);
  Multiplexer multiplexer_1 (.in0(AC), .in1(a3), .out(multiplexer_1_out), .sel(and_8_out));
  D_Flip_Flop d_ff_1 (.D(multiplexer_1_out), .clk(clock_1_out), .Q(AC));  // open: Qn, preset, reset
  Multiplexer multiplexer_2 (.in0(D0), .in1(a3), .out(multiplexer_2_out), .sel(and_9_out));
  D_Flip_Flop d_ff_2 (.D(multiplexer_2_out), .clk(clock_1_out), .Q(D0));  // open: Qn, preset, reset
  Multiplexer multiplexer_3 (.in0(D1), .in1(a3), .out(multiplexer_3_out), .sel(and_10_out));
  D_Flip_Flop d_ff_3 (.D(multiplexer_3_out), .clk(clock_1_out), .Q(D1));  // open: Qn, preset, reset
  Multiplexer multiplexer_4 (.in0(D2), .in1(a3), .out(multiplexer_4_out), .sel(and_11_out));
  D_Flip_Flop d_ff_4 (.D(multiplexer_4_out), .clk(clock_1_out), .Q(D2));  // open: Qn, preset, reset
  Multiplexer multiplexer_5 (.in0(D3), .in1(a3), .out(multiplexer_5_out), .sel(and_12_out));
  D_Flip_Flop d_ff_5 (.D(multiplexer_5_out), .clk(clock_1_out), .Q(D3));  // open: Qn, preset, reset
  Multiplexer multiplexer_6 (.in0(Engine), .in1(a3), .out(multiplexer_6_out), .sel(and_13_out));
  D_Flip_Flop d_ff_6 (.D(multiplexer_6_out), .clk(clock_1_out), .Q(Engine));  // open: Qn, preset, reset
  Multiplexer multiplexer_7 (.in0(Wipers), .in1(a3), .out(multiplexer_7_out), .sel(and_14_out));
  D_Flip_Flop d_ff_7 (.D(multiplexer_7_out), .clk(clock_1_out), .Q(Wipers));  // open: Qn, preset, reset
  and and_22 (and_22_out, and_1_out, undriven_2);
  not not_24 (not_24_out, and_22_out);
  and and_23 (and_23_out, and_2_out, undriven_2);
  not not_25 (not_25_out, and_23_out);
  and and_24 (and_24_out, and_3_out, undriven_2);
  not not_26 (not_26_out, and_24_out);
  and and_25 (and_25_out, and_4_out, undriven_2);
  not not_27 (not_27_out, and_25_out);
  and and_26 (and_26_out, and_5_out, undriven_2);
  not not_28 (not_28_out, and_26_out);
  and and_27 (and_27_out, and_6_out, undriven_2);
  not not_29 (not_29_out, and_27_out);
  and and_28 (and_28_out, and_7_out, undriven_2);
  not not_30 (not_30_out, and_28_out);
  nand nand_1 (nand_1_out, and_22_out, and_15_out);
  nand nand_2 (nand_2_out, and_15_out, not_24_out);
  nand nand_3 (nand_3_out, and_23_out, and_16_out);
  nand nand_4 (nand_4_out, and_16_out, not_25_out);
  nand nand_5 (nand_5_out, and_24_out, and_17_out);
  nand nand_6 (nand_6_out, and_17_out, not_26_out);
  nand nand_7 (nand_7_out, and_25_out, and_18_out);
  nand nand_8 (nand_8_out, and_18_out, not_27_out);
  nand nand_9 (nand_9_out, and_26_out, and_19_out);
  nand nand_10 (nand_10_out, and_19_out, not_28_out);
  nand nand_11 (nand_11_out, and_27_out, and_20_out);
  nand nand_12 (nand_12_out, and_20_out, not_29_out);
  nand nand_13 (nand_13_out, and_28_out, and_21_out);
  nand nand_14 (nand_14_out, and_21_out, not_30_out);
  not not_31 (not_31_out, and_1_out);
  nand nand_15 (nand_15_out, nand_1_out, nand_16_out);
  nand nand_16 (nand_16_out, nand_15_out, nand_2_out);
  nand nand_17 (nand_17_out, nand_3_out, nand_18_out);
  nand nand_18 (nand_18_out, nand_17_out, nand_4_out);
  nand nand_19 (nand_19_out, nand_5_out, nand_20_out);
  nand nand_20 (nand_20_out, nand_19_out, nand_6_out);
  nand nand_21 (nand_21_out, nand_7_out, nand_22_out);
  nand nand_22 (nand_22_out, nand_21_out, nand_8_out);
  nand nand_23 (nand_23_out, nand_9_out, nand_24_out);
  nand nand_24 (nand_24_out, nand_23_out, nand_10_out);
  nand nand_25 (nand_25_out, nand_11_out, nand_26_out);
  nand nand_26 (nand_26_out, nand_25_out, nand_12_out);
  nand nand_27 (nand_27_out, nand_13_out, nand_28_out);
  nand nand_28 (nand_28_out, nand_27_out, nand_14_out);
  and and_29 (and_29_out, nand_15_out, not_31_out);
  not not_32 (not_32_out, and_15_out);
  not not_33 (not_33_out, or_1_out);
  not not_34 (not_34_out, and_16_out);
  not not_35 (not_35_out, and_17_out);
  not not_36 (not_36_out, and_18_out);
  not not_37 (not_37_out, and_19_out);
  not not_38 (not_38_out, and_20_out);
  not not_39 (not_39_out, and_21_out);
  or or_1 (or_1_out, and_29_out, and_22_out);
  nand nand_29 (nand_29_out, or_1_out, not_32_out);
  nand nand_30 (nand_30_out, not_32_out, not_33_out);
  nand nand_31 (nand_31_out, nand_17_out, not_34_out);
  nand nand_32 (nand_32_out, not_34_out, nand_18_out);
  nand nand_33 (nand_33_out, nand_19_out, not_35_out);
  nand nand_34 (nand_34_out, not_35_out, nand_20_out);
  nand nand_35 (nand_35_out, nand_21_out, not_36_out);
  nand nand_36 (nand_36_out, not_36_out, nand_22_out);
  nand nand_37 (nand_37_out, nand_23_out, not_37_out);
  nand nand_38 (nand_38_out, not_37_out, nand_24_out);
  nand nand_39 (nand_39_out, nand_25_out, not_38_out);
  nand nand_40 (nand_40_out, not_38_out, nand_26_out);
  nand nand_41 (nand_41_out, nand_27_out, not_39_out);
  nand nand_42 (nand_42_out, not_39_out, nand_28_out);
  nand nand_43 (out_6, nand_29_out, nand_44_out);
  nand nand_44 (nand_44_out, nand_30_out, out_6);
  nand nand_45 (out_7, nand_31_out, nand_46_out);
  nand nand_46 (nand_46_out, nand_32_out, out_7);
  nand nand_47 (out_8, nand_33_out, nand_48_out);
  nand nand_48 (nand_48_out, nand_34_out, out_8);
  nand nand_49 (out_9, nand_35_out, nand_50_out);
  nand nand_50 (nand_50_out, nand_36_out, out_9);
  nand nand_51 (out_10, nand_37_out, nand_52_out);
  nand nand_52 (nand_52_out, nand_38_out, out_10);
  nand nand_53 (out_11, nand_39_out, nand_54_out);
  nand nand_54 (nand_54_out, nand_40_out, out_11);
  nand nand_55 (out_12, nand_41_out, nand_56_out);
  nand nand_56 (nand_56_out, nand_42_out, out_12);
endmodule
