// Logisim project prob1.circ as structural Verilog: 1 circuit, main circuit main
module main (
  input  [7:0] I1,
  input  [7:0] I2,
  input  [7:0] I3,
  input  [7:0] I4,
  input  [7:0] Address,
  input  [7:0] Control,
  input  [7:0] WriteDataSent,
  input  [7:0] RecievingData,
  input  [7:0] DataSent2,
  input  [7:0] DataSent,
  output [7:0] O1,
  output [7:0] O2,
  output [7:0] O3,
  output [7:0] O4,
  output [7:0] ReadDataReceived,
  output [7:0] out_16,
  output [7:0] out_17,
  output [7:0] DataRecieved,
  output [7:0] DataReceived2
);

  wire clk_out, decoder_1_out0, decoder_1_out1, decoder_1_out2, decoder_1_out3, decoder_1_out4,
       demultiplexer_1_out0, demultiplexer_1_out1, demultiplexer_1_out2, demultiplexer_1_out3, not_1_out,
       not_3_out, or_1_out;
  wire [7:0] controlled_buffer_4_out, controlled_buffer_5_out, controlled_buffer_6_out, demultiplexer_2_out0,
       demultiplexer_2_out1, demultiplexer_2_out2, demultiplexer_2_out3, multiplexer_1_out,
       multiplexer_2_out, multiplexer_3_out, not_2_out, not_4_out, ram_1_dout, rom_1_data;

  Decoder #(.enable("false"), .select(3)) decoder_1 (
    .out0(decoder_1_out0), .out1(decoder_1_out1), .out2(decoder_1_out2), .out3(decoder_1_out3),
    .out4(decoder_1_out4), .sel(Control[2:0]));  // open: out5, out6, out7
  assign ReadDataReceived = or_1_out ? out_16 : 8'bz;  // Controlled_Buffer controlled_buffer_1
  assign out_16 = not_1_out ? WriteDataSent : 8'bz;  // Controlled_Buffer controlled_buffer_2
  or or_1 (or_1_out, decoder_1_out0, decoder_1_out1, decoder_1_out3);
  not not_1 (not_1_out, or_1_out);
  RAM #(.enables("line"), .trigger("high")) ram_1 (
    .addr(Address), .we(decoder_1_out2), .clk(decoder_1_out2), .din(out_17), .dout(ram_1_dout));
  ROM rom_1 (.addr(Address), .data(rom_1_data));
  assign DataRecieved = RecievingData[7] ? controlled_buffer_4_out : 8'bz;  // Controlled_Buffer controlled_buffer_3
  assign controlled_buffer_4_out = not_2_out[7] ? DataSent : 8'bz;  // Controlled_Buffer controlled_buffer_4
  assign not_2_out = ~RecievingData;  // NOT_Gate not_2, 8 bits wide
  assign controlled_buffer_5_out = decoder_1_out1 ? ram_1_dout : 8'bz;  // Controlled_Buffer controlled_buffer_5
  assign controlled_buffer_6_out = decoder_1_out0 ? rom_1_data : 8'bz;  // Controlled_Buffer controlled_buffer_6
  Multiplexer #(.width(8)) multiplexer_1 (
    .in0(controlled_buffer_5_out), .in1(controlled_buffer_6_out), .out(multiplexer_1_out),
    .sel(decoder_1_out0));
  assign out_16 = or_1_out ? multiplexer_2_out : 8'bz;  // Controlled_Buffer ReadDataSent
  not not_3 (not_3_out, or_1_out);
  Multiplexer #(.width(8)) multiplexer_2 (
    .in0(multiplexer_1_out), .in1(multiplexer_3_out), .out(multiplexer_2_out), .sel(decoder_1_out3));
  assign out_17 = not_3_out ? out_16 : 8'bz;  // Controlled_Buffer WriteDataReceived
  Multiplexer #(.select(2), .width(8)) multiplexer_3 (
    .in0(I1), .in1(I2), .in2(I3), .in3(I4), .out(multiplexer_3_out), .sel(Address[1:0]));
  Demultiplexer #(.select(2)) demultiplexer_1 (
    .out0(demultiplexer_1_out0), .out1(demultiplexer_1_out1), .out2(demultiplexer_1_out2),
    .out3(demultiplexer_1_out3), .in(decoder_1_out4), .sel(Address[1:0]));
  Demultiplexer #(.select(2), .width(8)) demultiplexer_2 (
    .out0(demultiplexer_2_out0), .out1(demultiplexer_2_out1), .out2(demultiplexer_2_out2),
    .out3(demultiplexer_2_out3), .in(out_16), .sel(Address[1:0]));
  assign controlled_buffer_4_out = RecievingData[7] ? DataSent2 : 8'bz;  // Controlled_Buffer controlled_buffer_7
  assign DataReceived2 = not_4_out[0] ? controlled_buffer_4_out : 8'bz;  // Controlled_Buffer controlled_buffer_8
  assign not_4_out = ~RecievingData;  // NOT_Gate not_4, 8 bits wide
  Clock clk (.out(clk_out));
  Register register_1 (.D(demultiplexer_2_out0), .en(demultiplexer_1_out0), .clk(clk_out), .Q(O1));  // open: clr
  Register register_2 (.D(demultiplexer_2_out1), .en(demultiplexer_1_out1), .clk(clk_out), .Q(O2));  // open: clr
  Register register_3 (.D(demultiplexer_2_out2), .en(demultiplexer_1_out2), .clk(clk_out), .Q(O3));  // open: clr
  Register register_4 (.D(demultiplexer_2_out3), .en(demultiplexer_1_out3), .clk(clk_out), .Q(O4));  // open: clr

  // Notes on the sheet:
  //   0x0 -> Read from ROM
  //   0x1 -> Read from RAM
  //   0x10 -> Write to RAM
  //   0x11 -> Read from IO
  //   0x100 -> Write to IO
  //   reading data?
  //   contents of rom_1 (hex, n*v repeats v):
  //   0 0 f3
  //   5. write to IO
  //   1.read from ROM
  //   2. read from RAM
  //   3. write to RAM
  //   4. read from IO
  //   in case 4 or 5, tri state buffer to block sth?
endmodule
