// Logisim project CSCE312_milestone1_fetch.circ as structural Verilog: 10 circuits, main circuit RegisterFile
module main (
  input  [31:0] valM,
  input  [31:0] valE,
  output [31:0] valA,
  output [31:0] valB,
  output [3:0] icode,
  output [3:0] ifun,
  output [3:0] rA,
  output [3:0] rB,
  output [63:0] valC,
  output instr_valid
);

  wire clock_1_out, fetchunit_1_fetch_done, fetchunit_1_need_regids, fetchunit_1_need_valc;
  wire [3:0] registerfile_1_p1, registerfile_1_p3, registerfile_1_p4, registerfile_1_p6;
  wire [11:0] pc_1_pc_output, pcincrement_1_valp;

  Clock clock_1 (.out(clock_1_out));
  PC pc_1 (
    .fetch_done(fetchunit_1_fetch_done), .clk(clock_1_out), .valP(pcincrement_1_valp),
    .pc_output(pc_1_pc_output));
  FetchUnit fetchunit_1 (
    .clk(clock_1_out), .PC(pc_1_pc_output), .icode(icode), .ifun(ifun), .rA(rA), .rB(rB),
    .need_valC(fetchunit_1_need_valc), .need_regids(fetchunit_1_need_regids), .valC(valC),
    .fetch_done(fetchunit_1_fetch_done), .instr_valid(instr_valid));
  FetchUnit fetchunit_2 ();  // open: clk, PC, icode, ifun, rA, rB, need_valC, need_regids, valC, fetch_done, instr_valid
  PCIncrement pcincrement_1 (
    .need_valC(fetchunit_1_need_valc), .need_regids(fetchunit_1_need_regids), .in_3(pc_1_pc_output),
    .valP(pcincrement_1_valp));
  // RegisterFile registerfile_1: pin names not known; wires that end beside it: registerfile_1_p1, valA, registerfile_1_p3, registerfile_1_p4, valB, registerfile_1_p6, valM, valE
  dstE dste_1 (.icode(icode), .rB(rB), .dst_E(registerfile_1_p1));
  dstM dstm_1 (.icode(icode), .rA(rA), .dst_M(registerfile_1_p3));
  srcA srca_1 (.icode(icode), .rA(rA), .src_A(registerfile_1_p4));
  srcB srcb_1 (.icode(icode), .rB(rB), .src_B(registerfile_1_p6));
endmodule

module RegisterFile (
  input  clk,
  input  [7:0] valE,
  input  [3:0] srcA,
  input  [3:0] dstE,
  input  [3:0] srcB,
  input  [7:0] valM,
  input  [3:0] dstM,
  output [7:0] valA,
  output [7:0] valB
);

  wire decoder_1_out0, decoder_1_out1, decoder_1_out2, decoder_1_out3, decoder_1_out4, decoder_1_out5,
       decoder_1_out6, decoder_1_out7, decoder_1_out8, decoder_1_out9, decoder_1_out10, decoder_1_out11,
       decoder_1_out12, decoder_1_out13, decoder_1_out14, decoder_2_out0, decoder_2_out1, decoder_2_out2,
       decoder_2_out3, decoder_2_out4, decoder_2_out5, decoder_2_out6, decoder_2_out7, decoder_2_out8,
       decoder_2_out9, decoder_2_out10, decoder_2_out11, decoder_2_out12, decoder_2_out13, decoder_2_out14,
       or_1_out, or_2_out, or_3_out, or_4_out, or_5_out, or_6_out, or_7_out, or_8_out, or_9_out, or_10_out,
       or_11_out, or_12_out, or_13_out, or_14_out, or_15_out;
  wire [7:0] demultiplexer_1_out0, demultiplexer_1_out1, demultiplexer_1_out2, demultiplexer_1_out3,
       demultiplexer_1_out4, demultiplexer_1_out5, demultiplexer_1_out6, demultiplexer_1_out7,
       demultiplexer_1_out8, demultiplexer_1_out9, demultiplexer_1_out10, demultiplexer_1_out11,
       demultiplexer_1_out12, demultiplexer_1_out13, demultiplexer_1_out14, demultiplexer_2_out0,
       demultiplexer_2_out1, demultiplexer_2_out2, demultiplexer_2_out3, demultiplexer_2_out4,
       demultiplexer_2_out5, demultiplexer_2_out6, demultiplexer_2_out7, demultiplexer_2_out8,
       demultiplexer_2_out9, demultiplexer_2_out10, demultiplexer_2_out11, demultiplexer_2_out12,
       demultiplexer_2_out13, demultiplexer_2_out14, multiplexer_1_out, multiplexer_2_out, multiplexer_3_out,
       multiplexer_4_out, multiplexer_5_out, multiplexer_6_out, multiplexer_7_out, multiplexer_8_out,
       multiplexer_9_out, multiplexer_10_out, multiplexer_11_out, multiplexer_12_out, multiplexer_13_out,
       multiplexer_14_out, multiplexer_15_out, r8_q, r9_q, r10_q, r11_q, r12_q, r13_q, r14_q, r15_q, rax_q,
       rbp_q, rbx_q, rcx_q, rdi_q, rdx_q, rsi_q, rsp_q;

  Demultiplexer #(.select(4), .width(8)) demultiplexer_1 (
    .out0(demultiplexer_1_out0), .out1(demultiplexer_1_out1), .out2(demultiplexer_1_out2),
    .out3(demultiplexer_1_out3), .out4(demultiplexer_1_out4), .out5(demultiplexer_1_out5),
    .out6(demultiplexer_1_out6), .out7(demultiplexer_1_out7), .out8(demultiplexer_1_out8),
    .out9(demultiplexer_1_out9), .out10(demultiplexer_1_out10), .out11(demultiplexer_1_out11),
    .out12(demultiplexer_1_out12), .out13(demultiplexer_1_out13), .out14(demultiplexer_1_out14), .in(valM),
    .sel(dstM));  // open: out15
  Decoder #(.select(4)) decoder_1 (
    .out0(decoder_1_out0), .out1(decoder_1_out1), .out2(decoder_1_out2), .out3(decoder_1_out3),
    .out4(decoder_1_out4), .out5(decoder_1_out5), .out6(decoder_1_out6), .out7(decoder_1_out7),
    .out8(decoder_1_out8), .out9(decoder_1_out9), .out10(decoder_1_out10), .out11(decoder_1_out11),
    .out12(decoder_1_out12), .out13(decoder_1_out13), .out14(decoder_1_out14), .sel(dstM));  // open: out15, en
  Demultiplexer #(.select(4), .width(8)) demultiplexer_2 (
    .out0(demultiplexer_2_out0), .out1(demultiplexer_2_out1), .out2(demultiplexer_2_out2),
    .out3(demultiplexer_2_out3), .out4(demultiplexer_2_out4), .out5(demultiplexer_2_out5),
    .out6(demultiplexer_2_out6), .out7(demultiplexer_2_out7), .out8(demultiplexer_2_out8),
    .out9(demultiplexer_2_out9), .out10(demultiplexer_2_out10), .out11(demultiplexer_2_out11),
    .out12(demultiplexer_2_out12), .out13(demultiplexer_2_out13), .out14(demultiplexer_2_out14), .in(valE),
    .sel(dstE));  // open: out15
  Decoder #(.select(4)) decoder_2 (
    .out0(decoder_2_out0), .out1(decoder_2_out1), .out2(decoder_2_out2), .out3(decoder_2_out3),
    .out4(decoder_2_out4), .out5(decoder_2_out5), .out6(decoder_2_out6), .out7(decoder_2_out7),
    .out8(decoder_2_out8), .out9(decoder_2_out9), .out10(decoder_2_out10), .out11(decoder_2_out11),
    .out12(decoder_2_out12), .out13(decoder_2_out13), .out14(decoder_2_out14), .sel(dstE));  // open: out15, en
  Multiplexer #(.width(8)) multiplexer_1 (
    .in0(demultiplexer_2_out0), .in1(demultiplexer_1_out0), .out(multiplexer_1_out), .sel(decoder_1_out0));
  Multiplexer #(.width(8)) multiplexer_2 (
    .in0(demultiplexer_2_out1), .in1(demultiplexer_1_out1), .out(multiplexer_2_out), .sel(decoder_1_out1));
  Multiplexer #(.width(8)) multiplexer_3 (
    .in0(demultiplexer_2_out2), .in1(demultiplexer_1_out2), .out(multiplexer_3_out), .sel(decoder_1_out2));
  Multiplexer #(.width(8)) multiplexer_4 (
    .in0(demultiplexer_2_out3), .in1(demultiplexer_1_out3), .out(multiplexer_4_out), .sel(decoder_1_out3));
  Multiplexer #(.width(8)) multiplexer_5 (
    .in0(demultiplexer_2_out4), .in1(demultiplexer_1_out4), .out(multiplexer_5_out), .sel(decoder_1_out4));
  Multiplexer #(.width(8)) multiplexer_6 (
    .in0(demultiplexer_2_out5), .in1(demultiplexer_1_out5), .out(multiplexer_6_out), .sel(decoder_1_out5));
  Multiplexer #(.width(8)) multiplexer_7 (
    .in0(demultiplexer_2_out6), .in1(demultiplexer_1_out6), .out(multiplexer_7_out), .sel(decoder_1_out6));
  Multiplexer #(.width(8)) multiplexer_8 (
    .in0(demultiplexer_2_out7), .in1(demultiplexer_1_out7), .out(multiplexer_8_out), .sel(decoder_1_out7));
  Multiplexer #(.width(8)) multiplexer_9 (
    .in0(demultiplexer_2_out8), .in1(demultiplexer_1_out8), .out(multiplexer_9_out), .sel(decoder_1_out8));
  Multiplexer #(.width(8)) multiplexer_10 (
    .in0(demultiplexer_2_out9), .in1(demultiplexer_1_out9), .out(multiplexer_10_out), .sel(decoder_1_out9));
  Multiplexer #(.width(8)) multiplexer_11 (
    .in0(demultiplexer_2_out10), .in1(demultiplexer_1_out10), .out(multiplexer_11_out), .sel(decoder_1_out10));
  Multiplexer #(.width(8)) multiplexer_12 (
    .in0(demultiplexer_2_out11), .in1(demultiplexer_1_out11), .out(multiplexer_12_out), .sel(decoder_1_out11));
  Multiplexer #(.width(8)) multiplexer_13 (
    .in0(demultiplexer_2_out12), .in1(demultiplexer_1_out12), .out(multiplexer_13_out), .sel(decoder_1_out12));
  Multiplexer #(.width(8)) multiplexer_14 (
    .in0(demultiplexer_2_out13), .in1(demultiplexer_1_out13), .out(multiplexer_14_out), .sel(decoder_1_out13));
  Register rax (.D(multiplexer_1_out), .en(or_1_out), .clk(clk), .Q(rax_q));  // open: clr
  or or_1 (or_1_out, decoder_2_out0, decoder_1_out0);
  Register rcx (.D(multiplexer_2_out), .en(or_2_out), .clk(clk), .Q(rcx_q));  // open: clr
  or or_2 (or_2_out, decoder_2_out1, decoder_1_out0);
  Register rdx (.D(multiplexer_3_out), .en(or_3_out), .clk(clk), .Q(rdx_q));  // open: clr
  or or_3 (or_3_out, decoder_2_out2, decoder_1_out2);
  Register rbx (.D(multiplexer_4_out), .en(or_4_out), .clk(clk), .Q(rbx_q));  // open: clr
  or or_4 (or_4_out, decoder_2_out3, decoder_1_out3);
  Register rsp (.D(multiplexer_5_out), .en(or_5_out), .clk(clk), .Q(rsp_q));  // open: clr
  or or_5 (or_5_out, decoder_2_out4, decoder_1_out4);
  Register rbp (.D(multiplexer_6_out), .en(or_6_out), .clk(clk), .Q(rbp_q));  // open: clr
  or or_6 (or_6_out, decoder_2_out5, decoder_1_out5);
  Register rsi (.D(multiplexer_7_out), .en(or_7_out), .clk(clk), .Q(rsi_q));  // open: clr
  or or_7 (or_7_out, decoder_2_out6, decoder_1_out6);
  Register rdi (.D(multiplexer_8_out), .en(or_8_out), .clk(clk), .Q(rdi_q));  // open: clr
  or or_8 (or_8_out, decoder_2_out7, decoder_1_out7);
  Register r8 (.D(multiplexer_9_out), .en(or_9_out), .clk(clk), .Q(r8_q));  // open: clr
  or or_9 (or_9_out, decoder_2_out8, decoder_1_out8);
  Register r9 (.D(multiplexer_10_out), .en(or_10_out), .clk(clk), .Q(r9_q));  // open: clr
  or or_10 (or_10_out, decoder_2_out9, decoder_1_out9);
  Register r10 (.D(multiplexer_11_out), .en(or_11_out), .clk(clk), .Q(r10_q));  // open: clr
  or or_11 (or_11_out, decoder_2_out10, decoder_1_out10);
  Register r11 (.D(multiplexer_12_out), .en(or_12_out), .clk(clk), .Q(r11_q));  // open: clr
  or or_12 (or_12_out, decoder_2_out11, decoder_1_out11);
  Register r12 (.D(multiplexer_13_out), .en(or_13_out), .clk(clk), .Q(r12_q));  // open: clr
  or or_13 (or_13_out, decoder_2_out12, decoder_1_out12);
  Register r13 (.D(multiplexer_14_out), .en(or_14_out), .clk(clk), .Q(r13_q));  // open: clr
  or or_14 (or_14_out, decoder_2_out13, decoder_1_out13);
  Register r14 (.D(multiplexer_15_out), .en(or_15_out), .clk(clk), .Q(r14_q));  // open: clr
  Multiplexer #(.width(8)) multiplexer_15 (
    .in0(demultiplexer_2_out14), .in1(demultiplexer_1_out14), .out(multiplexer_15_out), .sel(decoder_1_out14));
  or or_15 (or_15_out, decoder_2_out14, decoder_1_out14);
  Register r15 (.Q(r15_q));  // open: D, en, clk, clr
  Multiplexer #(.select(4), .width(8)) multiplexer_16 (
    .in0(rax_q), .in1(rcx_q), .in2(rdx_q), .in3(rbx_q), .in4(rsp_q), .in5(rbp_q), .in6(rsi_q), .in7(rdi_q),
    .in8(r8_q), .in9(r9_q), .in10(r10_q), .in11(r11_q), .in12(r12_q), .in13(r13_q), .in14(r14_q),
    .in15(r15_q), .out(valA), .sel(srcA));
  Multiplexer #(.select(4), .width(8)) multiplexer_17 (
    .in0(rax_q), .in1(rcx_q), .in2(rdx_q), .in3(rbx_q), .in4(rsp_q), .in5(rbp_q), .in6(rsi_q), .in7(rdi_q),
    .in8(r8_q), .in9(r9_q), .in10(r10_q), .in11(r11_q), .in12(r12_q), .in13(r13_q), .in14(r14_q),
    .in15(r15_q), .out(valB), .sel(srcB));

  // Notes on the sheet:
  //   r15 should always remain 0
endmodule

module PC (
  input  [11:0] valP,
  input  fetch_done,
  input  clk,
  output [11:0] pc_output
);

  Register #(.width(12)) register_1 (.D(valP), .en(fetch_done), .clk(clk), .Q(pc_output));  // open: clr
endmodule

module FetchUnit (
  input  clk,
  input  [11:0] PC,
  output need_valC,
  output instr_valid,
  output need_regids,
  output [63:0] valC,
  output [3:0] icode,
  output [3:0] rA,
  output [3:0] ifun,
  output [3:0] rB,
  output fetch_done
);

  wire and_1_out, comparator_2_eq, comparator_4_eq, comparator_5_eq, comparator_6_eq, comparator_7_eq,
       comparator_8_eq, comparator_9_eq, comparator_10_eq, comparator_11_eq, comparator_12_eq,
       comparator_13_eq, comparator_14_eq, comparator_15_eq, decoder_1_out0, decoder_1_out1, decoder_1_out2,
       decoder_1_out3, decoder_1_out4, decoder_1_out5, decoder_1_out6, decoder_1_out7, decoder_1_out8,
       decoder_1_out9, valc_byte_en_1_byte_en, valc_byte_en_2_byte_en, valc_byte_en_3_byte_en,
       valc_byte_en_4_byte_en, valc_byte_en_5_byte_en, valc_byte_en_6_byte_en, valc_byte_en_7_byte_en,
       valc_byte_en_8_byte_en;
  wire [3:0] adder_1_out, adder_2_out, adder_4_out, bit_extender_1_out, byte_idx_q, multiplexer_1_out,
       multiplexer_2_out, multiplexer_3_out, subtractor_1_out;
  wire [7:0] controlled_buffer_1_out, controlled_buffer_2_out, rom_1_data;
  wire [11:0] adder_3_out, bit_extender_2_out;

  assign bit_extender_1_out = {{3{1'b0}}, need_regids};  // Bit_Extender bit_extender_1
  Register #(.width(4)) byte_idx (.D(multiplexer_2_out), .en(1'b1), .clk(clk), .Q(byte_idx_q));  // open: clr
  Multiplexer #(.width(4)) multiplexer_1 (.in0(4'b0000), .in1(4'b1000), .out(multiplexer_1_out), .sel(need_valC));
  Adder #(.width(4)) adder_1 (.a(bit_extender_1_out), .b(4'b0001), .out(adder_1_out));  // open: cin, cout
  Adder #(.width(4)) adder_2 (.a(multiplexer_1_out), .b(adder_1_out), .out(adder_2_out));  // open: cin, cout
  assign bit_extender_2_out = {{8{1'b0}}, byte_idx_q};  // Bit_Extender bit_extender_2
  Multiplexer #(.width(4)) multiplexer_2 (.in0(adder_4_out), .in1(4'b0000), .out(multiplexer_2_out), .sel(fetch_done));
  Subtractor #(.width(4)) subtractor_1 (.a(adder_2_out), .b(4'b0001), .out(subtractor_1_out));  // open: bin, bout
  Adder #(.width(12)) adder_3 (.a(PC), .b(bit_extender_2_out), .out(adder_3_out));  // open: cin, cout
  Adder #(.width(4)) adder_4 (.a(byte_idx_q), .b(4'b0001), .out(adder_4_out));  // open: cin, cout
  Comparator #(.mode("unsigned"), .width(4)) comparator_1 (
    .a(subtractor_1_out), .b(byte_idx_q), .eq(fetch_done));  // open: gt, lt
  ROM #(.addrWidth(12)) rom_1 (.addr(adder_3_out), .data(rom_1_data));
  Decoder #(.select(4)) decoder_1 (
    .out0(decoder_1_out0), .out1(decoder_1_out1), .out2(decoder_1_out2), .out3(decoder_1_out3),
    .out4(decoder_1_out4), .out5(decoder_1_out5), .out6(decoder_1_out6), .out7(decoder_1_out7),
    .out8(decoder_1_out8), .out9(decoder_1_out9), .sel(byte_idx_q), .en(1'b1));  // open: out10, out11, out12, out13, out14, out15
  Comparator #(.width(4)) comparator_2 (.a(byte_idx_q), .b(4'b0000), .eq(comparator_2_eq));  // open: gt, lt
  Comparator #(.mode("unsigned"), .width(4)) comparator_3 (
    .a(4'b1011), .b(multiplexer_3_out), .gt(instr_valid));  // open: eq, lt
  Multiplexer #(.width(4)) multiplexer_3 (
    .in0(icode), .in1(rom_1_data[7:4]), .out(multiplexer_3_out), .sel(comparator_2_eq));
  assign controlled_buffer_1_out = decoder_1_out0 ? rom_1_data : 8'bz;  // Controlled_Buffer controlled_buffer_1
  Register #(.width(4)) icode_reg (
    .D(controlled_buffer_1_out[7:4]), .en(decoder_1_out0), .clk(clk), .Q(icode));  // open: clr
  Register #(.width(4)) ifun_reg (
    .D(controlled_buffer_1_out[3:0]), .en(decoder_1_out0), .clk(clk), .Q(ifun));  // open: clr
  Comparator #(.mode("unsigned"), .width(4)) comparator_4 (
    .a(4'b1000), .b(multiplexer_3_out), .eq(comparator_4_eq));  // open: gt, lt
  Comparator #(.mode("unsigned"), .width(4)) comparator_5 (
    .a(4'b0111), .b(multiplexer_3_out), .eq(comparator_5_eq));  // open: gt, lt
  Comparator #(.mode("unsigned"), .width(4)) comparator_6 (
    .a(4'b0101), .b(multiplexer_3_out), .eq(comparator_6_eq));  // open: gt, lt
  Comparator #(.mode("unsigned"), .width(4)) comparator_7 (
    .a(4'b0100), .b(multiplexer_3_out), .eq(comparator_7_eq));  // open: gt, lt
  Comparator #(.mode("unsigned"), .width(4)) comparator_8 (
    .a(4'b0011), .b(multiplexer_3_out), .eq(comparator_8_eq));  // open: gt, lt
  Comparator #(.mode("unsigned"), .width(4)) comparator_9 (
    .a(4'b1011), .b(multiplexer_3_out), .eq(comparator_9_eq));  // open: gt, lt
  Comparator #(.mode("unsigned"), .width(4)) comparator_10 (
    .a(4'b1010), .b(multiplexer_3_out), .eq(comparator_10_eq));  // open: gt, lt
  Comparator #(.mode("unsigned"), .width(4)) comparator_11 (
    .a(4'b0110), .b(multiplexer_3_out), .eq(comparator_11_eq));  // open: gt, lt
  Comparator #(.mode("unsigned"), .width(4)) comparator_12 (
    .a(4'b0101), .b(multiplexer_3_out), .eq(comparator_12_eq));  // open: gt, lt
  Comparator #(.mode("unsigned"), .width(4)) comparator_13 (
    .a(4'b0100), .b(multiplexer_3_out), .eq(comparator_13_eq));  // open: gt, lt
  Comparator #(.mode("unsigned"), .width(4)) comparator_14 (
    .a(4'b0011), .b(multiplexer_3_out), .eq(comparator_14_eq));  // open: gt, lt
  Comparator #(.mode("unsigned"), .width(4)) comparator_15 (
    .a(4'b0010), .b(multiplexer_3_out), .eq(comparator_15_eq));  // open: gt, lt
  assign controlled_buffer_2_out = and_1_out ? rom_1_data : 8'bz;  // Controlled_Buffer controlled_buffer_2
  Register #(.width(4)) rA_reg (.D(controlled_buffer_2_out[7:4]), .en(and_1_out), .clk(clk), .Q(rA));  // open: clr
  and and_1 (and_1_out, need_regids, decoder_1_out1);
  or or_1 (need_valC, comparator_4_eq, comparator_5_eq, comparator_6_eq, comparator_7_eq, comparator_8_eq);
  or or_2 (need_regids, comparator_9_eq, comparator_11_eq, comparator_10_eq, comparator_12_eq, comparator_13_eq, comparator_14_eq, comparator_15_eq);
  Register #(.width(4)) rB_reg (.D(controlled_buffer_2_out[3:0]), .en(and_1_out), .clk(clk), .Q(rB));  // open: clr
  Register byte2 (.D(rom_1_data), .en(valc_byte_en_1_byte_en), .clk(clk), .Q(valC[7:0]));  // open: clr
  valC_byte_en valc_byte_en_1 (
    .need_valC(need_valC), .need_regids(need_regids), .d0(decoder_1_out2), .d1(decoder_1_out1),
    .byte_en(valc_byte_en_1_byte_en));
  Register byte3 (.D(rom_1_data), .en(valc_byte_en_2_byte_en), .clk(clk), .Q(valC[15:8]));  // open: clr
  valC_byte_en valc_byte_en_2 (
    .need_valC(need_valC), .need_regids(need_regids), .d0(decoder_1_out3), .d1(decoder_1_out2),
    .byte_en(valc_byte_en_2_byte_en));
  Register byte4 (.D(rom_1_data), .en(valc_byte_en_3_byte_en), .clk(clk), .Q(valC[23:16]));  // open: clr
  valC_byte_en valc_byte_en_3 (
    .need_valC(need_valC), .need_regids(need_regids), .d0(decoder_1_out4), .d1(decoder_1_out3),
    .byte_en(valc_byte_en_3_byte_en));
  Register byte5 (.D(rom_1_data), .en(valc_byte_en_4_byte_en), .clk(clk), .Q(valC[31:24]));  // open: clr
  valC_byte_en valc_byte_en_4 (
    .need_valC(need_valC), .need_regids(need_regids), .d0(decoder_1_out5), .d1(decoder_1_out4),
    .byte_en(valc_byte_en_4_byte_en));
  Register byte6 (.D(rom_1_data), .en(valc_byte_en_5_byte_en), .clk(clk), .Q(valC[39:32]));  // open: clr
  valC_byte_en valc_byte_en_5 (
    .need_valC(need_valC), .need_regids(need_regids), .d0(decoder_1_out6), .d1(decoder_1_out5),
    .byte_en(valc_byte_en_5_byte_en));
  Register byte7 (.D(rom_1_data), .en(valc_byte_en_6_byte_en), .clk(clk), .Q(valC[47:40]));  // open: clr
  valC_byte_en valc_byte_en_6 (
    .need_valC(need_valC), .need_regids(need_regids), .d0(decoder_1_out7), .d1(decoder_1_out6),
    .byte_en(valc_byte_en_6_byte_en));
  valC_byte_en valc_byte_en_7 (
    .need_valC(need_valC), .need_regids(need_regids), .d0(decoder_1_out8), .d1(decoder_1_out7),
    .byte_en(valc_byte_en_7_byte_en));
  Register byte8 (.D(rom_1_data), .en(valc_byte_en_7_byte_en), .clk(clk), .Q(valC[55:48]));  // open: clr
  Register byte9 (.D(rom_1_data), .en(valc_byte_en_8_byte_en), .clk(clk), .Q(valC[63:56]));  // open: clr
  valC_byte_en valc_byte_en_8 (
    .need_valC(need_valC), .need_regids(need_regids), .d0(decoder_1_out9), .d1(decoder_1_out8),
    .byte_en(valc_byte_en_8_byte_en));

  // Notes on the sheet:
  //   instr_len
  //   last_idx
  //   contents of rom_1 (hex, n*v repeats v):
  //   30 f0 8 7 6 5 4 3 2 1 20 3 10 70 a 7*0 10
  //   at_byte0
  //   icode_for_len
endmodule

module PCIncrement (
  input  need_valC,
  input  need_regids,
  input  [11:0] in_3,
  output [11:0] valP
);

  wire [11:0] adder_1_out, adder_2_out, bit_extender_1_out, multiplexer_1_out;

  Multiplexer #(.width(12)) multiplexer_1 (.in0({12{1'b0}}), .in1(12'h8), .out(multiplexer_1_out), .sel(need_valC));
  assign bit_extender_1_out = {{11{1'b0}}, need_regids};  // Bit_Extender bit_extender_1
  Adder #(.width(12)) adder_1 (.a(multiplexer_1_out), .b(bit_extender_1_out), .out(adder_1_out));  // open: cin, cout
  Adder #(.width(12)) adder_2 (.a(12'h1), .b(in_3), .out(adder_2_out));  // open: cin, cout
  Adder #(.width(12)) adder_3 (.a(adder_1_out), .b(adder_2_out), .out(valP));  // open: cin, cout
endmodule

module valC_byte_en (
  input  need_valC,
  input  need_regids,
  input  d0,
  input  d1,
  output byte_en
);

  wire and_1_out, and_2_out, not_1_out, or_1_out;

  not not_1 (not_1_out, need_regids);
  and and_1 (and_1_out, need_regids, d0);
  and and_2 (and_2_out, not_1_out, d1);
  or or_1 (or_1_out, and_1_out, and_2_out);
  and and_3 (byte_en, need_valC, or_1_out);

  // Notes on the sheet:
  //   orginal valC byte register
  //   register for jXX and call
endmodule

module dstM (
  input  [3:0] icode,
  input  [3:0] rA,
  output [3:0] dst_M
);
endmodule

module dstE (
  input  [3:0] icode,
  input  [3:0] rB,
  output [3:0] dst_E
);
endmodule

module srcA (
  input  [3:0] icode,
  input  [3:0] rA,
  output [3:0] src_A
);
endmodule

module srcB (
  input  [3:0] icode,
  input  [3:0] rB,
  output [3:0] src_B
);
endmodule
