// Logisim project Milestone1.circ as structural Verilog: 1 circuit, main circuit main
module main (
  input  [3:0] in_1,
  input  [3:0] in_2,
  input  [3:0] in_3,
  input  [3:0] in_4,
  input  [3:0] in_5,
  input  [3:0] in_6,
  input  [3:0] in_7,
  input  [11:0] in_8,
  input  [3:0] in_9,
  input  [3:0] in_10,
  input  [3:0] in_11,
  input  [3:0] in_12,
  input  [3:0] max_instr,
  input  [3:0] in_14,
  input  in_15,
  output need_valC,
  output need_regids,
  output instr_valid,
  output [63:0] valC,
  output [3:0] icode,
  output [3:0] ifun,
  output [3:0] rA,
  output [3:0] rB,
  output [7:0] icodeifun,
  output [23:0] align1,
  output [39:0] align2
);

  wire comparator_2_eq, comparator_3_eq, comparator_4_eq, comparator_5_eq, comparator_6_eq, comparator_7_eq,
       comparator_8_eq, comparator_9_eq, comparator_10_eq, comparator_11_eq, comparator_12_eq,
       comparator_13_eq;
  wire [11:0] adder_1_out, adder_2_out, bit_extender_1_out, bit_extender_2_out, Instruction_Memory_p1,
       multiplier_1_out;

  Comparator #(.mode("unsigned"), .width(4)) comparator_1 (.a(max_instr), .b(icode), .gt(instr_valid));  // open: eq, lt
  // ROM #(.addrWidth(12), .dataWidth(40), .line("dual")) Instruction_Memory: pin names not known; wires that end beside it: Instruction_Memory_p1, align2, {icode, ifun, rA, rB, align1}
  Register #(.width(12)) PC (.D(adder_2_out), .en(in_15), .Q(Instruction_Memory_p1));  // open: clk, clr
  Comparator #(.mode("unsigned"), .width(4)) comparator_2 (.a(in_1), .b(icode), .eq(comparator_2_eq));  // open: gt, lt
  Comparator #(.mode("unsigned"), .width(4)) comparator_3 (.a(in_2), .b(icode), .eq(comparator_3_eq));  // open: gt, lt
  Comparator #(.mode("unsigned"), .width(4)) comparator_4 (.a(in_3), .b(icode), .eq(comparator_4_eq));  // open: gt, lt
  Comparator #(.mode("unsigned"), .width(4)) comparator_5 (.a(in_4), .b(icode), .eq(comparator_5_eq));  // open: gt, lt
  Comparator #(.mode("unsigned"), .width(4)) comparator_6 (.a(in_5), .b(icode), .eq(comparator_6_eq));  // open: gt, lt
  Comparator #(.mode("unsigned"), .width(4)) comparator_7 (.a(in_6), .b(icode), .eq(comparator_7_eq));  // open: gt, lt
  Comparator #(.mode("unsigned"), .width(4)) comparator_8 (.a(in_7), .b(icode), .eq(comparator_8_eq));  // open: gt, lt
  Comparator #(.mode("unsigned"), .width(4)) comparator_9 (.a(in_9), .b(icode), .eq(comparator_9_eq));  // open: gt, lt
  Comparator #(.mode("unsigned"), .width(4)) comparator_10 (
    .a(in_10), .b(icode), .eq(comparator_10_eq));  // open: gt, lt
  Comparator #(.mode("unsigned"), .width(4)) comparator_11 (
    .a(in_11), .b(icode), .eq(comparator_11_eq));  // open: gt, lt
  Comparator #(.mode("unsigned"), .width(4)) comparator_12 (
    .a(in_12), .b(icode), .eq(comparator_12_eq));  // open: gt, lt
  Comparator #(.mode("unsigned"), .width(4)) comparator_13 (
    .a(in_14), .b(icode), .eq(comparator_13_eq));  // open: gt, lt
  or or_1 (need_valC, comparator_2_eq, comparator_3_eq, comparator_4_eq, comparator_5_eq, comparator_6_eq);
  or or_2 (need_regids, comparator_7_eq, comparator_9_eq, comparator_8_eq, comparator_10_eq, comparator_11_eq, comparator_12_eq, comparator_13_eq);
  assign bit_extender_1_out = {{11{need_valC}}, need_valC};  // Bit_Extender bit_extender_1
  Multiplier #(.width(12)) multiplier_1 (.a(in_8), .b(bit_extender_2_out), .out(multiplier_1_out));  // open: cin, cout
  assign bit_extender_2_out = {{11{need_regids}}, need_regids};  // Bit_Extender bit_extender_2
  Adder #(.width(12)) adder_1 (.a(bit_extender_1_out), .b(multiplier_1_out), .out(adder_1_out));  // open: cin, cout
  Adder #(.width(12)) adder_2 (.a(adder_1_out), .b(Instruction_Memory_p1), .out(adder_2_out));  // open: cin, cout

  assign valC = {align2, align1};

  // Notes on the sheet:
  //   in_8: initial=0x8
  //   max_instr: initial=0xb
  //   in_15: initial=0x1
  //   in_1: initial=0x8
  //   in_2: initial=0x7
  //   in_3: initial=0x5
  //   in_4: initial=0x4
  //   in_5: initial=0x3
  //   in_6: initial=0xb
  //   in_7: initial=0xa
  //   in_9: initial=0x6
  //   in_10: initial=0x5
  //   in_11: initial=0x4
  //   in_12: initial=0x3
  //   in_14: initial=0x2
  //   valC -> 3,4,5,7,8
  //   reg id -> a,b,6,5,4,3,2
  //   contents of Instruction_Memory (hex, n*v repeats v):
  //   20 11 13 13
endmodule
